# Fritzing sketch espfc_esp8266 (saved by Fritzing 0.9.3b)
circuit board: 7.23123cm x 7.13281cm

parts:
  U1 = NodeMCU V1.0
  C7 = Electrolytic Capacitor [capacitance=47µF package="100 mil [THT, electrolytic]"]
  C8 = Ceramic Capacitor [capacitance=100nF package="100 mil [THT, multilayer]"]
  J11 = Piezo Speaker
  PNP1 = PNP-Transistor [package="TO92 [THT]"]
  R4 = Resistor [tolerance=±5% resistance=2.2k package=THT]
  R5 = Resistor [tolerance=±5% resistance=22k package=THT]
  R6 = Resistor [tolerance=±5% resistance=4.7k package=THT]
  D2 = Rectifier Diode [part_number=1N4001 package="300 mil [THT]"]
  J18 = female pin header, 2 pins [form="♀ (female)"]
  Part1 = Triple Axis Accelerometer Breakout - ADXL345
  J20 = Dagu DGServo 9g header (male) [package=THT]
  J21 = Dagu DGServo 9g header (male) [package=THT]
  J24 = female pin header, 2 pins [form="♀ (female)"]
  C9 = Ceramic Capacitor [capacitance=100nF package="100 mil [THT, multilayer]"]
  J25 = Dagu DGServo 9g header (male) [package=THT]
  J26 = Dagu DGServo 9g header (male) [package=THT]
  J27 = female pin header, 2 pins [form="♀ (female)"]

nets:
  N1: U1.D0, R4.Pin_1
  N2: U1.D1, Part1.SCL
  N3: U1.D2, Part1.SDA
  3V3: U1.3V3, Part1.VCC, C9.1
  GND: U1.GND, C7.-, C8.0, R6.Pin_0, J18.pin1, Part1.GND, J20.gnd, J21.gnd, C9.0, J25.gnd, J26.gnd, J27.pin2
  N4: U1.D5, J21.pulse
  N5: U1.D6, J20.pulse
  N6: U1.D7, J25.pulse
  N7: U1.D8, J26.pulse
  N8: U1.RX, J24.pin1
  N9: U1.TX, J24.pin2
  VCC: U1.Vin, C7.+, C8.1, J11.pin2, PNP1.C, J20.Vcc, J21.Vcc, J25.Vcc, J26.Vcc, J27.pin1
  N10: U1.A0, R5.Pin_1, R6.Pin_1
  N11: J11.pin1, PNP1.E
  N12: PNP1.B, R4.Pin_0
  N13: R5.Pin_0, D2.cathode
  N14: D2.anode, J18.pin2

notes:
  D0 - Buzzer
  D1 - I2C, SCL
  D2 - I2C, SDA
  D4 - TX2, Blackbox
  D5 - PWM1
  D6 - PMW2
  D7 - PWM3
  D8 - PWM4
  RX - RX-PPM
  TX - TX
  GND
  3V
  A0 - ADC
  Blackbox
  RX-PPM
  PMW1
  PWM2
  PWM3
  PWM4
  Boop v2.0

custom parts:
  NodeMCU V1.0: ESP8266 based NodeMCU
  Triple Axis Accelerometer Breakout - ADXL345: Description: This new version adds 2 standoff holes as well as an extra decoupling capacitor. The ADXL345 is a small, thin, low power, 3-axis accelerometer with high resolution (13-bit) measurement at up to ±16 g. Digital output data is formatted as 16-bit twos complement and is accessible through either a SPI (3- or 4-wire) or I2C digital interface. The ADXL345 is well suited to measures the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
